# Fritzing sketch EspressoGuide (saved by Fritzing 0.9.2b)
stripboards: 1

parts:
  R1 = Resistor [tolerance=±5% resistance=220 package=THT]
  MV1 = MicroView [part_number=MicroView package="16pin wide"]
  Update_IF = female pin header, 5 pins [form="♀ (female)"]
  D1 = Rectifier Diode [part_number=1N4001 package="300 mil [THT]"]
  C1 = Ceramic Capacitor [capacitance=100nF package="100 mil [THT, multilayer]"]
  Power = female pin header, 2 pins [form="♀ (female)"]
  D2 = Rectifier Diode [part_number=1N4001 package="300 mil [THT]"]
  T1 = female pin header, 3 pins [form="♀ (female)"]
  C2 = Ceramic Capacitor [capacitance=100nF package="100 mil [THT, multilayer]"]
  D3 = Rectifier Diode [part_number=1N4001 package="300 mil [THT]"]  # not connected

nets:
  N1: R1.Pin_0, MV1.D2, C2.0
  N2: R1.Pin_1, T1.pin1
  N3: MV1.RESET, C1.0
  N4: MV1.GND, Update_IF.pin2, Power.pin2, T1.pin3, C2.1
  N5: MV1.RXD, Update_IF.pin4
  N6: MV1.TXD, Update_IF.pin3
  N7: MV1.D3, T1.pin2
  N8: MV1.Vin, D1.cathode, D2.cathode
  N9: Update_IF.pin1, D1.anode
  N10: Update_IF.pin5, C1.1
  N11: Power.pin1, D2.anode

custom parts:
  MicroView: MicroView - Chip-sized Arduino with OLED display.
